// Digital circuit vga.dig as structural Verilog
module vga (
  input  CLK,
  input  [9:0] _799,
  input  _1,
  input  [9:0] _96,
  input  [9:0] _144,
  input  [9:0] _784,
  input  [9:0] _524,
  input  _1_2,
  input  [9:0] _2,
  input  [9:0] _35,
  input  [9:0] _515,
  input  _0,
  input  R,
  input  B,
  input  G,
  output H_SYNC,
  output H_ACTIVE,
  output V_SYNC,
  output V_ACTIVE,
  output VIDEO_ACTIVE
);

  wire comparator_1_eq, comparator_1_gt, comparator_2_lt, comparator_3_lt, comparator_4_eq, comparator_4_gt,
       comparator_5_lt, comparator_6_lt, comparator_7_eq, comparator_8_eq, or_1_out, or_2_out;
  wire [9:0] H_COUNTER_out, V_COUNTER_out;

  Counter #(.Bits(10)) V_COUNTER (
    .en(_1_2), .C(comparator_7_eq), .clr(comparator_8_eq), .out(V_COUNTER_out));  // open: ovf
  Comparator #(.Bits(10)) comparator_1 (
    .a(V_COUNTER_out), .b(_35), .gt(comparator_1_gt), .eq(comparator_1_eq));  // open: lt
  Comparator #(.Bits(10)) comparator_2 (.a(V_COUNTER_out), .b(_515), .lt(comparator_2_lt));  // open: gt, eq
  Comparator #(.Bits(10)) comparator_3 (.a(H_COUNTER_out), .b(_96), .lt(comparator_3_lt));  // open: gt, eq
  Counter #(.Bits(10)) H_COUNTER (.en(_1), .C(CLK), .clr(comparator_7_eq), .out(H_COUNTER_out));  // open: ovf
  Comparator #(.Bits(10)) comparator_4 (
    .a(H_COUNTER_out), .b(_144), .gt(comparator_4_gt), .eq(comparator_4_eq));  // open: lt
  Comparator #(.Bits(10)) comparator_5 (.a(H_COUNTER_out), .b(_784), .lt(comparator_5_lt));  // open: gt, eq
  Comparator #(.Bits(10)) comparator_6 (.a(V_COUNTER_out), .b(_2), .lt(comparator_6_lt));  // open: gt, eq
  or or_1 (or_1_out, comparator_1_gt, comparator_1_eq);
  not not_1 (H_SYNC, comparator_3_lt);
  Comparator #(.Bits(10)) comparator_7 (.a(H_COUNTER_out), .b(_799), .eq(comparator_7_eq));  // open: gt, lt
  or or_2 (or_2_out, comparator_4_gt, comparator_4_eq);
  not not_2 (V_SYNC, comparator_6_lt);
  Comparator #(.Bits(10)) comparator_8 (.a(V_COUNTER_out), .b(_524), .eq(comparator_8_eq));  // open: gt, lt
  and and_1 (H_ACTIVE, or_2_out, comparator_5_lt);
  and and_2 (V_ACTIVE, or_1_out, comparator_2_lt);
  and and_3 (VIDEO_ACTIVE, H_ACTIVE, V_ACTIVE);
  Multiplexer multiplexer_1 (.sel(VIDEO_ACTIVE), .in_0(_0), .in_1(R));  // open: out
  Multiplexer multiplexer_2 (.sel(VIDEO_ACTIVE), .in_0(_0), .in_1(G));  // open: out
  Multiplexer multiplexer_3 (.sel(VIDEO_ACTIVE), .in_0(_0), .in_1(B));  // open: out

  // Notes on the sheet:
  //   _799: default 799
  //   _1: default 1
  //   _96: default 96
  //   _144: default 144
  //   _784: default 784
  //   _524: default 524
  //   _1_2: default 1
  //   _2: default 2
  //   _35: default 35
  //   _515: default 515
endmodule
